# Fritzing sketch arduino (saved by Fritzing 0.9.3b)
circuit board: 8.46667cm x 5.64444cm
breadboards: 1

parts:
  LM-35_Temperature_Sensor = LM35 Temperature Sensor [package="TO92 [THT]"]
  Part1 = Arduino Ethernet Shield (Rev3)
  Part2 = FC-28 Soil Hygrometer Module
  YL-83_-_Raining_Sensor = YL-83 Rain Sensor - Detection Board
  YL-83_-_Control_Board1 = YL-83 Rain Sensor - Control Board
  NodeMCU_ESP8266 = ESP8266 NodeMCU LoLin module
  FC-28_Humidity_Sensor = FC-28 Soil Hygrometer Module - Probe

nets:
  VCC: LM-35_Temperature_Sensor.+Vs, Part1.5V, Part2.VCC, YL-83_-_Control_Board1.VCC
  N1: LM-35_Temperature_Sensor.Vout, Part1.A1
  GND: LM-35_Temperature_Sensor.GND, Part1.GND, Part2.GND, YL-83_-_Control_Board1.GND, NodeMCU_ESP8266.GND
  N2: Part1.A0, Part2.AO
  N3: Part1.D2, NodeMCU_ESP8266.D1, NodeMCU_ESP8266.D6
  N4: Part1.PWM_D3, NodeMCU_ESP8266.D5
  N5: Part1.PWM_D5, YL-83_-_Control_Board1.AO
  N6: Part2.POS, FC-28_Humidity_Sensor.POS
  N7: Part2.NEG, FC-28_Humidity_Sensor.NEG
  N8: YL-83_-_Raining_Sensor.POS, YL-83_-_Control_Board1.POS
  N9: YL-83_-_Raining_Sensor.NEG, YL-83_-_Control_Board1.NEG

custom parts:
  FC-28 Soil Hygrometer Module: The FC-28 is a soil hygrometer module that uses the Texas Instruments LM393 comparator chip to provide an analog measurement of soil humidity. The digital output is high when soil moisture is over a certain threshold, as determined by adjusting the potentiometer.
  YL-83 Rain Sensor - Detection Board: The YL-83 is a rain sensor that has more resistance when dry and less resistance when wet. The module runs at 5V.
  YL-83 Rain Sensor - Control Board: The YL-83 is a rain sensor that has more resistance when dry and less resistance when wet. The module runs at 5V.
  ESP8266 NodeMCU LoLin module: ESP8266 based NodeMCU
  FC-28 Soil Hygrometer Module - Probe: The FC-28 is a soil hygrometer module that uses the Texas Instruments LM393 comparator chip to provide an analog measurement of soil humidity.
