# Fritzing sketch raspberry (saved by Fritzing 0.9.3b)
breadboards: 1

parts:
  Mod1 = Raspberry Pi Pico W
  R2 = Resistor [tolerance=±5% resistance=10k package=THT]
  LED3 = smd LED [color="Red (633nm)" package="0805 [SMD]"]
  Solenoid_Valve = Plastic Solenoid Valve
  Mod2 = Raspberry Pi Pico W
  Power_plug = Power plug
  Relay1 = Keyes Relay [package=THT]
  Relay = Keyes Relay [package=THT]

nets:
  N1: Mod1.pin_7, Relay1.signal
  N2: Mod1.pin_36, Relay1.power, Relay1.C
  N3: Mod1.pin_38, Mod1.pin_42, LED3.cathode, Relay1.ground
  N4: R2.Pin_0, Relay1.NO
  N5: R2.Pin_1, LED3.anode
  N6: Solenoid_Valve.no_name_yet#1, Relay.C
  N7: Solenoid_Valve.no_name_yet#2, Power_plug.GND
  N8: Mod2.pin_7, Relay.signal
  N9: Mod2.pin_36, Relay.power
  N10: Mod2.pin_38, Mod2.pin_42, Relay.ground
  N11: Power_plug.VCC, Relay.NO

custom parts:
  Raspberry Pi Pico W: Raspberry Pi Pico W. Based around the RP2040 microcontroller the Pico W is a low cost microcontroller device bringing Raspberry Pi quality, cost, and easy of use to the microcontroller space. The areas marked KEEPOUT in pcb silkscreen should not have traces running through them to avoid shorts on a soldered in module!
  Keyes Relay: The Keyes 5V relay module is suitable for SCM development, home appliance control. It uses a 5V~12V TIL control signal which can control DC / AC signal.
